# Fritzing sketch VendoAirPump (saved by Fritzing 0.9.5d)

parts:
  esp1 = ESP32 DevKitc V4
  J1 = Camdenboss CTB0158-2 [part_number=CTB0158-2 package=THT]
  S1 = SWITCH-MOMENTARY-2 [package=tactile-pth-12mm]
  S2 = SWITCH-MOMENTARY-2 [package=tactile-pth-12mm]
  S3 = SWITCH-MOMENTARY-2 [package=tactile-pth-12mm]
  S4 = SWITCH-MOMENTARY-2 [package=tactile-pth-12mm]
  A1 = 2957N11 pressure sensor
  M1 = 1 chan 5v relay module
  J2 = Camdenboss CTB0158-2 [part_number=CTB0158-2 package=THT]

nets:
  N1: esp1.IO16, M1.pin_3
  N2: esp1.IO17, S4.1
  N3: esp1.IO5, S3.1
  N4: esp1.IO18, S2.1
  N5: esp1.IO19, S1.1
  N6: esp1.GND, J1.pin2, S1.2, S2.2, S3.2, S4.2, A1.Pin_1, M1.pin_2
  N7: esp1.IO35, J1.pin1
  N8: esp1.IO32, A1.Pin_3
  N9: esp1.5V, A1.Pin_2, M1.pin_1
  N10: M1.pin_5, J2.pin2
  N11: M1.pin_6, J2.pin1

custom parts:
  ESP32 DevKitc V4: ESP32-DevKitC board with ESP32-WROOM-32 module. ESP32-DevKitC V4 is a small-sized ESP32-based development board produced by Espressif. Most of the pins on the ESP module are broken out to the pin headers on the board. The pins D0, D1, D2, D3, CMD and CLK are used internally for communication between ESP32 and SPI flash memory. They are grouped on both sides near the USB connector. Avoid using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
  2957N11 pressure sensor: Monitor and control vacuum pumps, air compressors, and hydraulics. These transmitters convert both pressure and vacuum into an electrical signal that can be interpreted by receiving devices, such as remote displays, programmable logic controllers, and motor speed controls.
  1 chan 5v relay module: 1 Channel 5V Relay Module Board Shield with Optocoupler Support High and Low Level Trigger for Arduino.
